# Fritzing sketch octalPointsense (saved by Fritzing 0.9.6b)
stripboards: 1

parts:
  J1 = Generic shrouded header - 10 pins [form="♂ (shrouded male)" package=THT]
  74LS1 = 74LS00 [package="DIP (Dual Inline) [THT]"]
  74LS2 = 74LS00 [package="DIP (Dual Inline) [THT]"]
  74LS3 = 74LS00 [package="DIP (Dual Inline) [THT]"]
  74LS4 = 74LS00 [package="DIP (Dual Inline) [THT]"]
  C1 = Ceramic Capacitor [capacitance=100nF voltage=35V package="100 mil [THT, multilayer]"]
  C2 = Ceramic Capacitor [capacitance=100nF voltage=35V package="100 mil [THT, multilayer]"]
  C3 = Ceramic Capacitor [capacitance=100nF voltage=35V package="100 mil [THT, multilayer]"]
  C4 = Ceramic Capacitor [capacitance=100nF voltage=35V package="100 mil [THT, multilayer]"]
  R1 = Resistor [tolerance=±5% power=0.25 resistance=10k package=THT]
  R2 = Resistor [tolerance=±5% power=0.25 resistance=10k package=THT]
  J2 = screw terminal, 3 pins
  J3 = screw terminal, 3 pins
  R3 = Resistor [tolerance=±5% power=0.25 resistance=1k package=THT]
  R4 = Resistor [tolerance=±5% power=0.25 resistance=10k package=THT]
  R5 = Resistor [tolerance=±5% power=0.25 resistance=10k package=THT]
  R6 = Resistor [tolerance=±5% power=0.25 resistance=1k package=THT]

nets:
  Line 8: J1.pin1
  Line 7: J1.pin2
  Line 6: J1.pin3
  Line 5: J1.pin4
  GND: J1.pin5, 74LS1.GND, 74LS2.GND, 74LS3.GND, 74LS4.GND, C1.0, C2.0, C3.0, C4.0, J2.pin2, J3.pin2
  5V: J1.pin6, 74LS1.Vcc, 74LS2.Vcc, 74LS3.Vcc, 74LS4.Vcc, C1.1, C2.1, C3.1, C4.1, R1.Pin_0, R2.Pin_0, R4.Pin_1, R5.Pin_1
  Line 4: J1.pin7
  Line 3: J1.pin8
  Line 2: J1.pin9, R6.Pin_1
  Line 1: J1.pin10, R3.Pin_0
  N1: 74LS1.1A, R1.Pin_1, J2.pin1
  N2: 74LS1.1B, 74LS1.2Y
  N3: 74LS1.1Y, 74LS1.2A, R3.Pin_1
  N4: 74LS1.2B, R2.Pin_1, J2.pin3
  N5: 74LS1.3Y, 74LS1.4A, R6.Pin_0
  N6: 74LS1.3A, J3.pin3, R5.Pin_0
  N7: 74LS1.3B, 74LS1.4Y
  N8: 74LS1.4B, J3.pin1, R4.Pin_0

custom parts:
  Generic shrouded header - 10 pins: Generic shrouded header
  74LS00: Quad 2-Input NAND Gate open drain/collector
